// Digital circuit ALU_Add_Sub.dig as structural Verilog
module ALU_Add_Sub (
  input  [7:0] A,
  input  [7:0] B,
  input  SUB,
  output [7:0] S
);

  wire [7:0] xor_1_out;

  xor xor_1 (xor_1_out[0], SUB, B[0]);
  xor xor_2 (xor_1_out[1], SUB, B[1]);
  xor xor_3 (xor_1_out[2], SUB, B[2]);
  xor xor_4 (xor_1_out[3], SUB, B[3]);
  xor xor_5 (xor_1_out[4], SUB, B[4]);
  xor xor_6 (xor_1_out[5], SUB, B[5]);
  xor xor_7 (xor_1_out[6], SUB, B[6]);
  xor xor_8 (xor_1_out[7], SUB, B[7]);
  adder_8bit adder_8bit_1 (.A(A), .B(xor_1_out), .Cin(SUB), .S(S));  // open: Cout
endmodule
