// Digital circuit ALU_v1.dig as structural Verilog
module ALU_v1 (
  input  [7:0] A_in,
  input  [7:0] B_in,
  input  [1:0] Op_Sel,
  output [7:0] S
);

  wire [7:0] multiplexer_1_out;

  Multiplexer #(.Bits(8)) multiplexer_1 (.sel(Op_Sel[1]), .in_0(B_in), .in_1(8'h1), .out(multiplexer_1_out));
  ALU_Add_Sub alu_add_sub_1 (.A(A_in), .B(multiplexer_1_out), .SUB(Op_Sel[0]), .S(S));
endmodule
