// Digital circuit CPU_main.dig as structural Verilog
module CPU_main (
  input  clk
);

  wire Acc_in, Acc_out, ALU_busy, ALU_out, and_2_out, and_3_out, B_reg_in, CLR_T, comparator_1_eq,
       comparator_2_eq, IR_driver, IR_in, IR_out, MAR_in, MEM_out, not_1_out, PC_enable, PC_ld, PC_load,
       PC_out, RESET, START, Z_FLAG, Z_flag_t;
  wire [2:0] ALU_Op, COUNTER;
  wire [3:0] IR_q, OPCODE;
  wire [7:0] Acc_f, alu_main_1_s_out, and_1_out, B_reg_q, Display_adder, MAR_q, multiplexer_1_out, not_2_out,
       PC_out_2, W_BUS;

  // Probe on COUNTER
  // Probe on OPCODE
  // Probe on clk
  CounterPreset #(.Bits(8)) PC (
    .en(PC_enable), .C(clk), .dir(1'b0), .in(W_BUS), .ld(PC_ld), .clr(RESET), .out(PC_out_2));  // open: ovf
  // Probe on {OPCODE, COUNTER}
  // Probe on {OPCODE, COUNTER}
  assign W_BUS = PC_out ? PC_out_2 : 8'bz;  // Driver driver_1
  // Probe PC_PROBE on PC_out_2
  ROM #(.AddrBits(7), .Bits(16)) CONTROL_ROM (
    .A({OPCODE, COUNTER}), .sel(1'b1),
    .D({ALU_Op, PC_out, MAR_in, MEM_out, IR_in, IR_out, Acc_in, Acc_out, ALU_out, B_reg_in, PC_enable, PC_load, CLR_T, START}));
  Button u_RESET (.out(RESET));
  // Probe on RESET
  // Probe on {ALU_Op, PC_out, MAR_in, MEM_out, IR_in, IR_out, Acc_in, Acc_out, ALU_out, B_reg_in, PC_enable, PC_load, CLR_T, START}
  // Probe on ALU_Op
  not not_1 (not_1_out, ALU_busy);
  Register #(.Bits(8)) IR (.D(W_BUS), .C(clk), .en(IR_in), .Q({OPCODE, IR_q}));
  // Probe on ALU_out
  // Probe on IR_out
  // Probe on MEM_out
  // Probe on PC_out
  Counter #(.Bits(3)) u_Counter (.en(not_1_out), .C(clk), .clr(CLR_T), .out(COUNTER));  // open: ovf
  assign and_1_out = {OPCODE, IR_q} & 8'hf;  // And and_1, 8 bits wide
  // Probe on {OPCODE, IR_q}
  Register #(.Bits(8)) MAR (.D(W_BUS), .C(clk), .en(MAR_in), .Q(MAR_q));
  // Probe on COUNTER
  // Probe on OPCODE
  // Probe on OPCODE
  // Probe on and_1_out
  assign W_BUS = IR_driver ? and_1_out : 8'bz;  // Driver driver_2
  // Probe MAR_PROBE on MAR_q
  // Probe on MAR_q
  // Probe on Acc_f
  // Probe on W_BUS
  EEPROMDualPort #(.AddrBits(8), .Bits(8)) eepromdualport_1 (
    .A(MAR_q), .Din(W_BUS), .str(START), .C(clk), .ld(MEM_out), .D(W_BUS));
  Register #(.Bits(8)) B_reg (.D(W_BUS), .C(clk), .en(B_reg_in), .Q(B_reg_q));
  Register #(.Bits(8)) Acc (.D(W_BUS), .C(clk), .en(Acc_in), .Q(Acc_f));
  // Probe on Acc_f
  // Probe on B_reg_q
  // Probe on W_BUS
  assign not_2_out = ~Acc_f;  // Not not_2, 8 bits wide
  ALU_main alu_main_1 (
    .A_in(Acc_f), .B_in(B_reg_q), .ALU_op(ALU_Op), .CLK(clk), .START(START), .S_out(alu_main_1_s_out),
    .Z_flag(Z_FLAG), .ALU_busy(ALU_busy));
  assign W_BUS = Acc_out ? Acc_f : 8'bz;  // Driver driver_3
  // Probe on Acc_f[7]
  Multiplexer #(.Bits(8)) multiplexer_1 (.sel(Acc_f[7]), .in_0(Acc_f), .in_1(Display_adder), .out(multiplexer_1_out));
  adder_8bit adder_8bit_1 (.A(not_2_out), .B({8{1'b0}}), .Cin(1'b1), .S(Display_adder));  // open: Cout
  assign W_BUS = ALU_out ? alu_main_1_s_out : 8'bz;  // Driver driver_4
  Seven_Seg seven_seg_1 (.a(1'b0), .b(1'b0), .c(1'b0), .d(1'b0), .e(1'b0), .f(1'b0), .g(Acc_f[7]), .dp(1'b0));
  // Probe on multiplexer_1_out
  Seven_Seg_Hex seven_seg_hex_1 (.d(Acc_f[7:4]), .dp(1'b0));
  and and_2 (and_2_out, Z_flag_t, PC_load);
  Comparator #(.Bits(4)) comparator_1 (.a(OPCODE), .b(4'b0100), .eq(comparator_1_eq));  // open: gt, lt
  and and_3 (and_3_out, Z_flag_t, IR_out);
  Comparator #(.Bits(4)) comparator_2 (.a(OPCODE), .b(4'b0100), .eq(comparator_2_eq));  // open: gt, lt
  Register register_1 (.D(Z_FLAG), .C(clk), .en(START), .Q(Z_flag_t));
  Multiplexer multiplexer_2 (.sel(comparator_1_eq), .in_0(PC_load), .in_1(and_2_out), .out(PC_ld));
  Multiplexer multiplexer_3 (.sel(comparator_2_eq), .in_0(IR_out), .in_1(and_3_out), .out(IR_driver));
  Seven_Seg_Hex seven_seg_hex_2 (.d(Acc_f[3:0]), .dp(1'b0));

  // Other names for the same wires on the sheet: SIGN_BIT = Acc_f[7]

  // Notes on the sheet:
  //   clk: Hz: 2
  //   contents of CONTROL_ROM (hex, n*v repeats v):
  //   1800,8,600,900,480,2,0,0,1800,8,600,900,410,a0,2,0,1800,8,600
  //   ,900,41,2,0,0,1800,8,600,104,2,0,0,0,1800,8,600,104,2,0,0,0,1800
  //   ,8,600,900,410,8001,80a0,2,1800,8,600,900,410,a001,a0a0,2,1800
  //   ,8,600,900,410,20a1,2,0,1800,8,600,40a0,2,0,0,0,1800,8,600,60a0,2
  //   contents of eepromdualport_1 (hex, n*v repeats v):
  //   a,7a,45,b,34,c,36,4*0,ee,fb
endmodule
