// Digital circuit counter_4bit.dig as structural Verilog
module counter_4bit (
  input  [3:0] D,
  input  CLK,
  input  LOAD,
  input  EN,
  output [3:0] Q,
  output ZERO
);

  CounterPreset #(.Bits(4)) counterpreset_1 (
    .en(EN), .C(CLK), .dir(1'b1), .in(D), .ld(LOAD), .clr(1'b0), .out(Q));  // open: ovf
  nor nor_1 (ZERO, Q[0], Q[1], Q[2], Q[3]);
endmodule
