// Digital circuit divider_4bit.dig as structural Verilog
module divider_4bit (
  input  [3:0] A_in,
  input  [3:0] B_in,
  input  Clk,
  output [3:0] Q_out,
  output [3:0] R_out
);

  wire and_3_out, comparator_1_eq, comparator_1_gt, INIT, IS_R_GTE_B, LOOP, not_1_out, not_2_out, or_1_out,
       or_2_out, START, START_LATCHED, STATE;
  wire [3:0] adder_4bit_1_sum, B_reg_q, multiplexer_1_out, multiplexer_2_out, sub_4bits_1_s;

  not not_1 (not_1_out, STATE);
  and and_1 (INIT, not_1_out, START_LATCHED);
  and and_2 (LOOP, STATE, IS_R_GTE_B);
  or or_1 (or_1_out, INIT, LOOP);
  Button u_START (.out(START));
  RS_FF_AS rs_ff_as_1 (.S(START), .R(STATE), .Q(START_LATCHED));  // open: nQ
  D_FF d_ff_1 (.D(or_1_out), .C(Clk), .Q(STATE));  // open: nQ
  or or_2 (or_2_out, INIT, LOOP);
  Multiplexer #(.Bits(4)) multiplexer_1 (.sel(INIT), .in_0(sub_4bits_1_s), .in_1(A_in), .out(multiplexer_1_out));
  Multiplexer #(.Bits(4)) multiplexer_2 (.sel(INIT), .in_0(adder_4bit_1_sum), .in_1(4'b0000), .out(multiplexer_2_out));
  Register #(.Bits(4)) R_reg (.D(multiplexer_1_out), .C(Clk), .en(or_2_out), .Q(R_out));
  Register #(.Bits(4)) B_reg (.D(B_in), .C(Clk), .en(INIT), .Q(B_reg_q));
  Register #(.Bits(4)) Q_reg (.D(multiplexer_2_out), .C(Clk), .en(or_2_out), .Q(Q_out));
  not not_2 (not_2_out, IS_R_GTE_B);
  sub_4bits sub_4bits_1 (.A(R_out), .B(B_reg_q), .S(sub_4bits_1_s));  // open: Bo
  and and_3 (and_3_out, STATE, not_2_out);
  Comparator #(.Bits(4)) comparator_1 (.a(R_out), .b(B_reg_q), .gt(comparator_1_gt), .eq(comparator_1_eq));  // open: lt
  adder_4bit adder_4bit_1 (.A(Q_out), .B(4'b0001), .Sum(adder_4bit_1_sum));  // open: Cout
  LED DONE (.in(and_3_out));
  or or_3 (IS_R_GTE_B, comparator_1_gt, comparator_1_eq);
endmodule
