// Digital circuit multiplier_4bit.dig as structural Verilog
module multiplier_4bit (
  input  [3:0] A_in,
  input  [3:0] B_in,
  input  CLK,
  input  START,
  output [7:0] P_out
);

  wire and_3_out, BUSY, COUNTER_NOT_ZERO, EN_P, INIT, not_1_out, not_2_out, START_t, STATE;
  wire [3:0] A_reg_q, counterpreset_1_out;
  wire [7:0] adder_8bit_1_s, multiplexer_1_out;

  not not_1 (not_1_out, STATE);
  and and_1 (INIT, not_1_out, START_t);
  and and_2 (BUSY, STATE, COUNTER_NOT_ZERO);
  or or_1 (EN_P, INIT, BUSY);
  Button START_BUTTON ();  // open: out
  RS_FF_AS rs_ff_as_1 (.S(START), .R(STATE), .Q(START_t));  // open: nQ
  D_FF d_ff_1 (.D(EN_P), .C(CLK), .Q(STATE));  // open: nQ
  Register #(.Bits(4)) A_reg (.D(A_in), .C(CLK), .en(INIT), .Q(A_reg_q));
  CounterPreset #(.Bits(4)) counterpreset_1 (
    .en(BUSY), .C(CLK), .dir(1'b1), .in(B_in), .ld(INIT), .clr(1'b0), .out(counterpreset_1_out));  // open: ovf
  Multiplexer #(.Bits(8)) multiplexer_1 (.sel(INIT), .in_0(adder_8bit_1_s), .in_1({8{1'b0}}), .out(multiplexer_1_out));
  Register #(.Bits(8)) P_reg (.D(multiplexer_1_out), .C(CLK), .en(EN_P), .Q(P_out));
  adder_8bit adder_8bit_1 (.A(P_out), .B({4'b0000, A_reg_q}), .Cin(1'b0), .S(adder_8bit_1_s));  // open: Cout
  or or_2 (COUNTER_NOT_ZERO, counterpreset_1_out[0], counterpreset_1_out[1], counterpreset_1_out[2], counterpreset_1_out[3]);
  not not_2 (not_2_out, COUNTER_NOT_ZERO);
  and and_3 (and_3_out, STATE, not_2_out);
  LED DONE (.in(and_3_out));
endmodule
