// Digital circuit sub_4bits.dig as structural Verilog
module sub_4bits (
  input  [3:0] A,
  input  [3:0] B,
  output [3:0] S,
  output Bo
);

  wire [3:0] adder_4bit_1_sum, not_1_out;

  assign not_1_out = ~B;  // Not not_1, 4 bits wide
  adder_4bit adder_4bit_1 (.A(not_1_out), .B(4'b0001), .Sum(adder_4bit_1_sum));  // open: Cout
  adder_4bit adder_4bit_2 (.A(A), .B(adder_4bit_1_sum), .Sum(S), .Cout(Bo));
endmodule
